# Fritzing sketch diagrama (saved by Fritzing 0.9.9b)
breadboards: 1

parts:
  Relay_5V1 = Keyes Relay [package=THT]
  U1 = NodeMCU V1.0
  R1 = Resistor [tolerance=±5% power=0.25 resistance=220 package=THT]
  LED1 = LED - 5mm [color="Red (633nm)" current=0.030 package="5 mm [THT]"]
  R2 = Resistor [tolerance=±5% power=0.25 resistance=220 package=THT]
  LED2 = LED - 5mm [color="Yellow (595nm)" current=0.030 package="5 mm [THT]"]

nets:
  N1: Relay_5V1.signal, U1.D5, LED1.anode
  N2: Relay_5V1.power, U1.Vin
  N3: Relay_5V1.ground, U1.GND, R1.Pin_1, R2.Pin_1
  N4: U1.D6, LED2.anode
  N5: R1.Pin_0, LED1.cathode
  N6: R2.Pin_0, LED2.cathode

custom parts:
  Keyes Relay: The Keyes 5V relay module is suitable for SCM development, home appliance control. It uses a 5V~12V TIL control signal which can control DC / AC signal.
  NodeMCU V1.0: ESP8266 based NodeMCU
